// Logisim project main_pomysly.circ as structural Verilog: 1 circuit, main circuit main
module main (
  input  in_1,
  input  in_2,
  input  [23:0] in_3,
  input  [23:0] in_4,
  input  [23:0] in_5,
  input  [23:0] in_6,
  input  [23:0] in_7,
  input  [23:0] in_8,
  input  [23:0] in_9,
  input  [23:0] in_10
);

  wire A, CLK_ANIM, CLK_IN, clock_1_out, D, d_ff_1_q, d_ff_1_qn, Display_ready, Key_impulse,
       keyboard_1_avail, main_7_clk_out, main_8_clk_out, main_9_clk_out, Main_clk_out, not_1_out, RESET,
       RstRgr, Start_Stop, TIMEOUT;
  wire [1:0] key;
  wire [2:0] and_2_out, and_3_out, bit_extender_1_out, bit_extender_2_out, Counter, divider_1_rem,
       random_1_out, SR1, SR2, SR3, SR4, SR5;
  wire [3:0] H1, H2, H3, H4;
  wire [6:0] keyboard_1_data, register_1_q;
  wire [23:0] main_6_output, main_7_o0, main_7_o1, main_7_o2, main_7_o3, main_7_o4, main_7_o5, main_7_o6,
       main_7_o7, main_7_register_out, main_8_o0, main_8_o1, main_8_o2, main_8_o3, main_8_o4, main_8_o5,
       main_8_o6, main_8_o7, main_8_register_out, main_9_o0, main_9_o1, main_9_o2, main_9_o3, main_9_o4,
       main_9_o5, main_9_o6, main_9_o7, main_9_register_out, main_10_o0, main_10_o1, main_10_o2, main_10_o3,
       main_10_o4, main_10_o5, main_10_o6, main_10_o7, main_11_o1, main_11_o2, main_11_o2_2, main_11_o2_3,
       main_11_o2_4, main_11_o2_5, main_11_o2_6, main_11_o2_7, multiplexer_1_out, or_1_out, RegOut, ROM0,
       ROM1, ROM2, rom_1_data, rom_2_data;
  wire [31:0] Timer;

  Button button_1 (.out(Start_Stop));
  Button button_2 (.out(RESET));
  DotMatrix #(.matrixcols(32), .matrixrows(1)) dotmatrix_1 (
    .col0(Timer[31]), .col1(Timer[30]), .col2(Timer[29]), .col3(Timer[28]), .col4(Timer[27]),
    .col5(Timer[26]), .col6(Timer[25]), .col7(Timer[24]), .col8(Timer[23]), .col9(Timer[22]),
    .col10(Timer[21]), .col11(Timer[20]), .col12(Timer[19]), .col13(Timer[18]), .col14(Timer[17]),
    .col15(Timer[16]), .col16(Timer[15]), .col17(Timer[14]), .col18(Timer[13]), .col19(Timer[12]),
    .col20(Timer[11]), .col21(Timer[10]), .col22(Timer[9]), .col23(Timer[8]), .col24(Timer[7]),
    .col25(Timer[6]), .col26(Timer[5]), .col27(Timer[4]), .col28(Timer[3]), .col29(Timer[2]),
    .col30(Timer[1]), .col31(Timer[0]));
  Clock #(.highDuration(4), .lowDuration(4)) Animation_clk (.out(CLK_ANIM));
  Clock Main_clk (.out(Main_clk_out));
  D_Flip_Flop d_ff_1 (.clk(Start_Stop), .D(d_ff_1_qn), .Q(d_ff_1_q), .Qn(d_ff_1_qn));  // open: preset, en, reset
  Hex_Digit_Display hex_digit_display_1 (.value(H4));  // open: dp
  and and_1 (CLK_IN, Main_clk_out, d_ff_1_q);
  Hex_Digit_Display hex_digit_display_2 (.value(H2));  // open: dp
  Hex_Digit_Display hex_digit_display_3 (.value(H3));  // open: dp
  PointCounter_main main_1 (.ADD(CLK_IN), .RESET(RESET), .X000(H4), ._0X00(H3), ._00X0(H2), ._000X(H1));  // open: LIMIT
  TIMEDISPLAY_main main_2 (
    .WHEN_1__SUB_TIME_ONE_TICK__WHEN_0_ADD_TIME_ON_TICK(in_2), .CLK(CLK_IN), .RESET(RESET),
    .OutputScreen(Timer), .TIME_OUT(TIMEOUT));
  Hex_Digit_Display hex_digit_display_4 (.value(H1));  // open: dp
  Stop_countera_main main_3 (.Clk(CLK_ANIM), .Reset(Key_impulse), .Counter(Counter));
  assign bit_extender_1_out = {{2{D}}, D};  // Bit_Extender bit_extender_1
  assign bit_extender_2_out = {{2{A}}, A};  // Bit_Extender bit_extender_2
  assign and_2_out = Counter & bit_extender_1_out;  // AND_Gate and_2, 3 bits wide
  assign and_3_out = Counter & bit_extender_2_out;  // AND_Gate and_3, 3 bits wide
  ROM_Tree_main main_4 (.Counter(Counter), .ROM_0(ROM0), .ROM_1(ROM1), .ROM_2(ROM2));
  Clock clock_1 (.out(clock_1_out));
  ROM #(.addrWidth(3), .dataWidth(24)) rom_1 (.addr(and_2_out), .data(rom_1_data));  // open: sel
  ROM #(.addrWidth(3), .dataWidth(24)) rom_2 (.addr(and_3_out), .data(rom_2_data));  // open: sel
  Random #(.width(3)) random_1 (.clk(clock_1_out), .out(random_1_out));  // open: next, clr
  Shift_register_rom_control_main main_5 (
    .in_1(ROM0), .in_2(ROM1), .in_3(ROM2), .Output(RegOut), .Address(SR1));  // open: in_4, in_5, in_6, in_7, in_8
  Multiplexer #(.select(2), .width(24)) multiplexer_1 (
    .in1(rom_1_data), .in2(rom_2_data), .out(multiplexer_1_out), .sel(key));  // open: in0, in3, en
  Divider #(.width(3)) divider_1 (.a(random_1_out), .b(3'b011), .rem(divider_1_rem));  // open: out, upper
  Shift_register_rom_control_main main_6 (
    .in_1(ROM0), .in_2(ROM1), .in_3(ROM2), .Output(main_6_output), .Address(SR5));  // open: in_4, in_5, in_6, in_7, in_8
  Shift_Register #(.width(3), .length(5)) shift_register_1 (
    .shift(in_1), .in(divider_1_rem), .clk(Key_impulse), .q0(SR1), .q1(SR2), .q2(SR3), .q3(SR4), .q4(SR5));  // open: out, load, clr, d0, d1, d2, d3, d4
  assign or_1_out = main_6_output | multiplexer_1_out;  // OR_Gate or_1, 24 bits wide
  Screen_animation_segment_main main_7 (
    .Input_line(RegOut), .Impulse(Key_impulse), .Reset(RstRgr), .O0(main_7_o0), .O1(main_7_o1),
    .O2(main_7_o2), .Register_out(main_7_register_out), .O3(main_7_o3), .O4(main_7_o4), .O5(main_7_o5),
    .O6(main_7_o6), .O7(main_7_o7), .Clk_out(main_7_clk_out), .Clk(CLK_ANIM));
  DotMatrix #(.inputtype("row"), .matrixcols(24), .matrixrows(8)) dotmatrix_2 (
    .row0(main_7_o0), .row1(main_7_o1), .row2(main_7_o2), .row3(main_7_o3), .row4(main_7_o4),
    .row5(main_7_o5), .row6(main_7_o6), .row7(main_7_o7));
  Screen_animation_segment_main main_8 (
    .Input_line(main_7_register_out), .Impulse(Key_impulse), .Reset(RstRgr), .O0(main_8_o0), .O1(main_8_o1),
    .O2(main_8_o2), .Register_out(main_8_register_out), .O3(main_8_o3), .O4(main_8_o4), .O5(main_8_o5),
    .O6(main_8_o6), .O7(main_8_o7), .Clk_out(main_8_clk_out), .Clk(main_7_clk_out));
  DotMatrix #(.inputtype("row"), .matrixcols(24), .matrixrows(8)) dotmatrix_3 (
    .row0(main_8_o0), .row1(main_8_o1), .row2(main_8_o2), .row3(main_8_o3), .row4(main_8_o4),
    .row5(main_8_o5), .row6(main_8_o6), .row7(main_8_o7));
  Screen_animation_segment_main main_9 (
    .Input_line(main_8_register_out), .Impulse(Key_impulse), .Reset(RstRgr), .O0(main_9_o0), .O1(main_9_o1),
    .O2(main_9_o2), .Register_out(main_9_register_out), .O3(main_9_o3), .O4(main_9_o4), .O5(main_9_o5),
    .O6(main_9_o6), .O7(main_9_o7), .Clk_out(main_9_clk_out), .Clk(main_8_clk_out));
  DotMatrix #(.inputtype("row"), .matrixcols(24), .matrixrows(8)) dotmatrix_4 (
    .row0(main_9_o0), .row1(main_9_o1), .row2(main_9_o2), .row3(main_9_o3), .row4(main_9_o4),
    .row5(main_9_o5), .row6(main_9_o6), .row7(main_9_o7));
  Screen_animation_segment_main main_10 (
    .Input_line(main_9_register_out), .Impulse(Key_impulse), .Reset(RstRgr), .O0(main_10_o0),
    .O1(main_10_o1), .O2(main_10_o2), .O3(main_10_o3), .O4(main_10_o4), .O5(main_10_o5), .O6(main_10_o6),
    .O7(main_10_o7), .Clk(main_9_clk_out));  // open: Register_out, Clk_out
  DotMatrix #(.inputtype("row"), .matrixcols(24), .matrixrows(8)) dotmatrix_5 (
    .row0(main_10_o0), .row1(main_10_o1), .row2(main_10_o2), .row3(main_10_o3), .row4(main_10_o4),
    .row5(main_10_o5), .row6(main_10_o6), .row7(main_10_o7));
  DotMatrix #(.inputtype("row"), .matrixcols(24), .matrixrows(8)) dotmatrix_6 (
    .row0(main_11_o1), .row1(main_11_o2), .row2(main_11_o2_2), .row3(main_11_o2_3), .row4(main_11_o2_4),
    .row5(main_11_o2_5), .row6(main_11_o2_6), .row7(main_11_o2_7));
  Display_first_segment_control_main main_11 (
    .In(or_1_out), .Clk(CLK_IN), .Reset(RstRgr), .Counter(Counter), .O1(main_11_o1), .O2(main_11_o2),
    .O2_2(main_11_o2_2), .O2_3(main_11_o2_3), .O2_4(main_11_o2_4), .O2_5(main_11_o2_5), .O2_6(main_11_o2_6),
    .O2_7(main_11_o2_7), .Display_ready(Display_ready));
  not not_1 (not_1_out, Display_ready);
  Pull_Resistor pull_resistor_1 (.node(Key_impulse));
  assign Key_impulse = keyboard_1_avail ? CLK_IN : 1'bz;  // Controlled_Buffer controlled_buffer_1
  Keyboard keyboard_1 (
    .clk(Key_impulse), .re(Display_ready), .clr(not_1_out), .avail(keyboard_1_avail), .data(keyboard_1_data));
  // Probe on in_3
  // Probe on in_4
  // Probe on in_5
  // Probe on in_8
  Button Reset_display_register (.out(RstRgr));
  DotMatrix #(.inputtype("row"), .matrixcols(24), .matrixrows(8)) dotmatrix_7 (
    .row0(in_3), .row1(in_4), .row2(in_5), .row3(in_8), .row4(in_6), .row5(in_9), .row6(in_7), .row7(in_10));
  // Probe on in_6
  // Probe on in_9
  Register #(.width(7)) register_1 (.D(keyboard_1_data), .Q(register_1_q), .clk(Key_impulse));  // open: en, clr
  Key_recognition_main main_12 (.Keyboard_input(register_1_q), .Out(key), .Clk(CLK_IN), .A(A), .D(D));
  // Probe on in_7
  // Probe on in_10

  // Other names for the same wires on the sheet: _1[23:0] = in_3; _2[23:0] = in_4; _3[23:0] = in_5; _4[23:0] = in_8;
  //   _5[23:0] = in_6; _6[23:0] = in_9; _7[23:0] = in_7; _8[23:0] = in_10

  // Notes on the sheet:
  //   contents of rom_1 (hex, n*v repeats v):
  //   0 c cc de 7e 4e c 33
  //   contents of rom_2 (hex, n*v repeats v):
  //   0 300000 330000 7b0000 7e0000 720000 300000 cc0000
endmodule
